# Fritzing sketch extra ch sch (saved by Fritzing 0.9.4)
breadboards: 2

parts:
  Parça1 = Arduino Nano (Rev3.0)
  R1 = Resistor [tolerance=±5% resistance=10k package=THT]
  S1 = Pushbutton [package=THT]
  R2 = Resistor [tolerance=±5% resistance=10k package=THT]
  S2 = Pushbutton [package=THT]
  R3 = Resistor [tolerance=±5% resistance=10k package=THT]
  S3 = Pushbutton [package=THT]
  R4 = Resistor [tolerance=±5% resistance=10k package=THT]
  S4 = Pushbutton [package=THT]
  R5 = Resistor [tolerance=±5% resistance=10k package=THT]
  S5 = Pushbutton [package=THT]
  R6 = Resistor [tolerance=±5% resistance=10k package=THT]
  S6 = Pushbutton [package=THT]
  R7 = Resistor [tolerance=±5% resistance=10k package=THT]
  S7 = Pushbutton [package=THT]
  R8 = Resistor [tolerance=±5% resistance=10k package=THT]
  S8 = Pushbutton [package=THT]
  R9 = Trimmer Potentiometer [maximum_resistance=10kΩ package=THT]
  R10 = Trimmer Potentiometer [maximum_resistance=10kΩ package=THT]
  R11 = Trimmer Potentiometer [maximum_resistance=10kΩ package=THT]
  R12 = Trimmer Potentiometer [maximum_resistance=10kΩ package=THT]
  SG1 = Buzzer 12mm [package=buzzer-ccv-kit]
  R13 = Trimmer Potentiometer [maximum_resistance=10kΩ package=THT]
  R14 = Trimmer Potentiometer [maximum_resistance=10kΩ package=THT]
  R15 = Resistor [tolerance=±5% resistance=220 package=THT]
  R16 = Resistor [tolerance=±5% resistance=220 package=THT]
  S9 = Pushbutton [package=THT]
  S10 = Pushbutton [package=THT]

nets:
  N1: Parça1.GND, R9.leg1, R10.leg1, R11.leg1, R12.leg1, SG1.2
  N2: Parça1.D2, R1.Pin_1, S1.leg0
  N3: Parça1.D3, R2.Pin_1, S2.leg0
  N4: Parça1.D4, R8.Pin_1, S8.leg0
  N5: Parça1.D5, R3.Pin_1, S3.leg0
  N6: Parça1.D6, R4.Pin_1, S4.leg0
  N7: Parça1.D7, R5.Pin_1, S5.leg0
  N8: Parça1.D8, R6.Pin_1, S6.leg0
  N9: Parça1.D9, R7.Pin_1, S7.leg0
  N10: Parça1.D12/MISO, SG1.1
  N11: Parça1.5V, S1.leg1, S2.leg1, S3.leg1, S4.leg1, S5.leg1, S6.leg1, S7.leg1, S8.leg1, R9.leg2, R10.leg2, R11.leg2, R12.leg2, R13.leg2, R14.leg2, S9.leg1, S10.leg1
  N12: Parça1.A5, R14.wiper
  N13: Parça1.A4, R13.wiper
  N14: Parça1.A3, R12.wiper
  N15: Parça1.A2, R11.wiper
  N16: Parça1.A1, R10.wiper
  N17: Parça1.A0, R9.wiper
  N18: Parça1.D13/SCK, R15.Pin_1, S9.leg0
  N19: R1.Pin_0, R2.Pin_0, R3.Pin_0, R4.Pin_0, R5.Pin_0, R6.Pin_0, R7.Pin_0, R8.Pin_0, R13.leg1, R14.leg1, R15.Pin_0, R16.Pin_0
  N20: R16.Pin_1, S10.leg0

notes:
  Signal Out
  Buzzer
  POTS: AIL - ELE - THR - RUD
  Buttons: RUD- RUD+ THR- THR+ ELE- ELE+ AIL- AIL+
  10K Resistor for pulldown
  AUX4 AUX3 AUX2 AUX1
  SW4 SW3 SW2 SW1
